# Fritzing sketch Hello_Functions_Fritzing (saved by Fritzing 0.9.3b)
breadboards: 1

parts:
  Part1 = Arduino Uno (Rev3)
  J1 = Basic Servo
  HC-SR04_Sensor_1 = HC-SR04 Ultrasonic Distance Sensor  # not connected

nets:
  N1: Part1.D3_PWM, J1.pulse
